// Logisim project Lab4.circ as structural Verilog: 12 circuits, main circuit main
module main (
);

  wire alu_control_1_alusrc, and_1_out, clock_1_out, comparator_1_eq, controlcircuit_1_branch,
       controlcircuit_1_memread, controlcircuit_1_memtoreg, controlcircuit_1_memwrite,
       controlcircuit_1_regwrite;
  wire [3:0] alu_control_1_aluctrl0;
  wire [31:0] adder_1_out, adder_2_out, datamemory_1_readdata, immgen_1_imm32,
       instructionmemory_1_instruction, multiplexer_1_out, multiplexer_2_out, multiplexer_3_out,
       register_1_q, registerfile_1_rdata1, registerfile_1_rdata2, thirty_bit_alu_1_result;

  Register #(.width(32)) register_1 (
    .D(multiplexer_2_out), .en(1'b1), .clk(clock_1_out), .Q(register_1_q));  // open: clr
  Clock clock_1 (.out(clock_1_out));
  Adder #(.width(32)) adder_1 (.a(register_1_q), .b(32'h4), .out(adder_1_out));  // open: cin, cout
  InstructionMemory instructionmemory_1 (
    .Address(register_1_q[23:0]), .ClockIn(clock_1_out), .Instruction(instructionmemory_1_instruction));
  ALU_Control alu_control_1 (
    .i30(instructionmemory_1_instruction[30]), .i14(instructionmemory_1_instruction[14]),
    .i13(instructionmemory_1_instruction[13]), .i12(instructionmemory_1_instruction[12]),
    .i6(instructionmemory_1_instruction[6]), .i5(instructionmemory_1_instruction[5]),
    .i4(instructionmemory_1_instruction[4]), .aluCtrl3(alu_control_1_aluctrl0[3]),
    .aluCtrl2(alu_control_1_aluctrl0[2]), .aluCtrl1(alu_control_1_aluctrl0[1]),
    .aluCtrl0(alu_control_1_aluctrl0[0]), .aluSrc(alu_control_1_alusrc));
  ControlCircuit controlcircuit_1 (
    .I6(instructionmemory_1_instruction[6]), .I5(instructionmemory_1_instruction[5]),
    .I4(instructionmemory_1_instruction[4]), .I3(instructionmemory_1_instruction[3]),
    .I2(instructionmemory_1_instruction[2]), .I1(instructionmemory_1_instruction[1]),
    .I0(instructionmemory_1_instruction[0]), .MemToReg(controlcircuit_1_memtoreg),
    .RegWrite(controlcircuit_1_regwrite), .MemRead(controlcircuit_1_memread),
    .MemWrite(controlcircuit_1_memwrite), .Branch(controlcircuit_1_branch));
  registerFile registerfile_1 (
    .RReg1(instructionmemory_1_instruction[19:15]), .RReg2(instructionmemory_1_instruction[24:20]),
    .WData(multiplexer_3_out), .Clock_in(clock_1_out), .Write(controlcircuit_1_regwrite),
    .WReg(instructionmemory_1_instruction[11:7]), .RData1(registerfile_1_rdata1),
    .RData2(registerfile_1_rdata2));
  ImmGen immgen_1 (.Instruction(instructionmemory_1_instruction), .IMM32(immgen_1_imm32));
  Multiplexer #(.enable("false"), .width(32)) multiplexer_1 (
    .in0(registerfile_1_rdata2), .in1(immgen_1_imm32), .out(multiplexer_1_out), .sel(alu_control_1_alusrc));
  Adder #(.width(32)) adder_2 (.a(register_1_q), .b(immgen_1_imm32), .out(adder_2_out));  // open: cin, cout
  Comparator #(.width(32)) comparator_1 (
    .a(registerfile_1_rdata1), .b(registerfile_1_rdata2), .eq(comparator_1_eq));  // open: gt, lt
  thirty_bit_ALU thirty_bit_alu_1 (
    .ALU_Ctrl(alu_control_1_aluctrl0), .A(registerfile_1_rdata1), .B(multiplexer_1_out),
    .Result(thirty_bit_alu_1_result));  // open: C_Out
  and and_1 (and_1_out, controlcircuit_1_branch, comparator_1_eq);
  Multiplexer #(.enable("false"), .width(32)) multiplexer_2 (
    .in0(adder_1_out), .in1(adder_2_out), .out(multiplexer_2_out), .sel(and_1_out));
  DataMemory datamemory_1 (
    .Adress(thirty_bit_alu_1_result[25:0]), .MemWrite(controlcircuit_1_memwrite),
    .MemRead(controlcircuit_1_memread), .ClockIn(clock_1_out), .WriteData(registerfile_1_rdata2),
    .ReadData(datamemory_1_readdata));
  Multiplexer #(.enable("false"), .width(32)) multiplexer_3 (
    .in0(thirty_bit_alu_1_result), .in1(datamemory_1_readdata), .out(multiplexer_3_out),
    .sel(controlcircuit_1_memtoreg));
endmodule

module InstructionMemory (
  input  [23:0] Address,
  input  ClockIn,
  output [31:0] Instruction
);

  wire not_1_out;

  not not_1 (not_1_out, ClockIn);
  RAM #(.addrWidth(22), .asyncread("true"), .dataWidth(32)) ram_1 (
    .addr(Address[23:2]), .we(1'b0), .oe(not_1_out), .dout(Instruction));  // open: clk, din
endmodule

module DataMemory (
  input  [25:0] Adress,
  input  MemWrite,
  input  MemRead,
  input  ClockIn,
  input  [31:0] WriteData,
  output [31:0] ReadData
);

  RAM #(.addrWidth(24), .asyncread("true"), .dataWidth(32)) ram_1 (
    .addr(Adress[25:2]), .we(MemWrite), .oe(MemRead), .clk(ClockIn), .din(WriteData), .dout(ReadData));
endmodule

module ImmGen (
  input  [31:0] Instruction,
  output [31:0] IMM32
);

  Multiplexer #(.enable("false"), .width(4)) multiplexer_1 (
    .in0(Instruction[24:21]), .in1(Instruction[11:8]), .out(IMM32[4:1]), .sel(Instruction[5]));
  Multiplexer #(.enable("false")) multiplexer_2 (
    .in0(Instruction[31]), .in1(Instruction[7]), .out(IMM32[11]), .sel(Instruction[6]));
  assign IMM32[31:12] = {{19{Instruction[31]}}, Instruction[31]};  // Bit_Extender bit_extender_1
  Multiplexer #(.enable("false"), .select(2)) multiplexer_3 (
    .in0(Instruction[20]), .in1(Instruction[7]), .in3(1'b0), .out(IMM32[0]), .sel(Instruction[6:5]));  // open: in2

  assign IMM32[10:5] = Instruction[30:25];

  // Other names for the same wires on the sheet: I30_25[5:0] = Instruction[30:25]; I5 = Instruction[5];
  //   I6_5[1:0] = Instruction[6:5]; I6 = Instruction[6]; I7 = Instruction[7]; I11_8[3:0] = Instruction[11:8];
  //   I_20 = Instruction[20]; I24_21[3:0] = Instruction[24:21]; I31 = Instruction[31]
endmodule

module ControlCircuit (
  input  I6,
  input  I5,
  input  I4,
  input  I3,
  input  I2,
  input  I1,
  input  I0,
  output MemToReg,
  output RegWrite,
  output MemRead,
  output MemWrite,
  output Branch
);

  wire not_1_out, not_2_out, not_3_out;

  not not_1 (not_1_out, I6);
  not not_2 (not_2_out, I5);
  not not_3 (not_3_out, I4);
  and and_1 (MemToReg, not_2_out, not_3_out);
  or or_1 (RegWrite, not_2_out, I4);
  and and_2 (MemRead, not_2_out, not_3_out);
  and and_3 (MemWrite, not_1_out, I5, not_3_out);

  assign Branch = I6;
endmodule

module register_file_four (
  input  [1:0] Reg1,
  input  [1:0] Reg2,
  input  [31:0] WData,
  input  Clock_In,
  input  Write,
  input  [1:0] WReg,
  output [31:0] out_7,
  output [31:0] out_8
);

  wire demultiplexer_1_out0, demultiplexer_1_out1, demultiplexer_1_out2, demultiplexer_1_out3;
  wire [31:0] register_1_q, register_2_q, register_3_q, register_4_q;

  Demultiplexer #(.enable("false"), .select(2)) demultiplexer_1 (
    .out0(demultiplexer_1_out0), .out1(demultiplexer_1_out1), .out2(demultiplexer_1_out2),
    .out3(demultiplexer_1_out3), .in(Write), .sel(WReg));
  Register #(.width(32)) register_1 (
    .D(WData), .en(demultiplexer_1_out0), .clk(Clock_In), .Q(register_1_q), .clr(Write));
  Register #(.width(32)) register_2 (
    .D(WData), .en(demultiplexer_1_out1), .clk(Clock_In), .Q(register_2_q));  // open: clr
  Register #(.width(32)) register_3 (
    .D(WData), .en(demultiplexer_1_out2), .clk(Clock_In), .Q(register_3_q));  // open: clr
  Register #(.width(32)) register_4 (
    .D(WData), .en(demultiplexer_1_out3), .clk(Clock_In), .Q(register_4_q));  // open: clr
  Multiplexer #(.enable("false"), .select(2), .width(32)) multiplexer_1 (
    .in0(register_1_q), .in1(register_2_q), .in2(register_3_q), .in3(register_4_q), .out(out_7), .sel(Reg1));
  Multiplexer #(.enable("false"), .select(2), .width(32)) multiplexer_2 (
    .in0(register_1_q), .in1(register_2_q), .in2(register_3_q), .in3(register_4_q), .out(out_8), .sel(Reg2));
endmodule

module registerFile (
  input  [4:0] RReg1,
  input  [4:0] RReg2,
  input  [31:0] WData,
  input  Clock_in,
  input  Write,
  input  [4:0] WReg,
  output [31:0] RData1,
  output [31:0] RData2
);

  wire W3_0, W7_4, W11_8, W15_12, W19_16, W23_20, W27_24, W31_28;
  wire [31:0] register_file_four_1_out_7, register_file_four_1_out_8, register_file_four_2_out_7,
       register_file_four_2_out_8, register_file_four_3_out_7, register_file_four_3_out_8,
       register_file_four_4_out_7, register_file_four_4_out_8, register_file_four_5_out_7,
       register_file_four_5_out_8, register_file_four_6_out_7, register_file_four_6_out_8,
       register_file_four_7_out_7, register_file_four_7_out_8, register_file_four_8_out_7,
       register_file_four_8_out_8;

  Demultiplexer #(.enable("false"), .select(3)) demultiplexer_1 (
    .out0(W3_0), .out1(W7_4), .out2(W11_8), .out3(W15_12), .out4(W19_16), .out5(W23_20), .out6(W27_24),
    .out7(W31_28), .in(Write), .sel(WReg[4:2]));
  register_file_four register_file_four_1 (
    .Reg1(RReg1[1:0]), .Reg2(RReg2[1:0]), .WData(WData), .Clock_In(Clock_in), .Write(W3_0), .WReg(WReg[1:0]),
    .out_7(register_file_four_1_out_7), .out_8(register_file_four_1_out_8));
  register_file_four register_file_four_2 (
    .Reg1(RReg1[1:0]), .Reg2(RReg2[1:0]), .WData(WData), .Clock_In(Clock_in), .Write(W7_4), .WReg(WReg[1:0]),
    .out_7(register_file_four_2_out_7), .out_8(register_file_four_2_out_8));
  register_file_four register_file_four_3 (
    .Reg1(RReg1[1:0]), .Reg2(RReg2[1:0]), .WData(WData), .Clock_In(Clock_in), .Write(W11_8),
    .WReg(WReg[1:0]), .out_7(register_file_four_3_out_7), .out_8(register_file_four_3_out_8));
  register_file_four register_file_four_4 (
    .Reg1(RReg1[1:0]), .Reg2(RReg2[1:0]), .WData(WData), .Clock_In(Clock_in), .Write(W15_12),
    .WReg(WReg[1:0]), .out_7(register_file_four_4_out_7), .out_8(register_file_four_4_out_8));
  register_file_four register_file_four_5 (
    .Reg1(RReg1[1:0]), .Reg2(RReg2[1:0]), .WData(WData), .Clock_In(Clock_in), .Write(W19_16),
    .WReg(WReg[1:0]), .out_7(register_file_four_5_out_7), .out_8(register_file_four_5_out_8));
  register_file_four register_file_four_6 (
    .Reg1(RReg1[1:0]), .Reg2(RReg2[1:0]), .WData(WData), .Clock_In(Clock_in), .Write(W23_20),
    .WReg(WReg[1:0]), .out_7(register_file_four_6_out_7), .out_8(register_file_four_6_out_8));
  register_file_four register_file_four_7 (
    .Reg1(RReg1[1:0]), .Reg2(RReg2[1:0]), .WData(WData), .Clock_In(Clock_in), .Write(W27_24),
    .WReg(WReg[1:0]), .out_7(register_file_four_7_out_7), .out_8(register_file_four_7_out_8));
  register_file_four register_file_four_8 (
    .Reg1(RReg1[1:0]), .Reg2(RReg2[1:0]), .WData(WData), .Clock_In(Clock_in), .Write(W31_28),
    .WReg(WReg[1:0]), .out_7(register_file_four_8_out_7), .out_8(register_file_four_8_out_8));
  Multiplexer #(.enable("false"), .select(3), .width(32)) multiplexer_1 (
    .in0(register_file_four_1_out_7), .in1(register_file_four_2_out_7), .in2(register_file_four_3_out_7),
    .in3(register_file_four_4_out_7), .in4(register_file_four_5_out_7), .in5(register_file_four_6_out_7),
    .in6(register_file_four_7_out_7), .in7(register_file_four_8_out_7), .out(RData1), .sel(RReg1[4:2]));
  Multiplexer #(.enable("false"), .select(3), .width(32)) multiplexer_2 (
    .in0(register_file_four_1_out_8), .in1(register_file_four_2_out_8), .in2(register_file_four_3_out_8),
    .in3(register_file_four_4_out_8), .in4(register_file_four_5_out_8), .in5(register_file_four_6_out_8),
    .in6(register_file_four_7_out_8), .in7(register_file_four_8_out_8), .out(RData2), .sel(RReg2[4:2]));
endmodule

module one_bit_ALU (
  input  [3:0] ALU_Ctrl,
  input  A,
  input  B,
  input  C_in,
  output R,
  output C_out
);

  wire and_1_out, multiplexer_1_out, not_1_out, one_bit_adder_1_s, or_1_out, xor_1_out;

  not not_1 (not_1_out, B);
  Multiplexer #(.enable("false")) multiplexer_1 (.in0(B), .in1(not_1_out), .out(multiplexer_1_out), .sel(ALU_Ctrl[2]));
  and and_1 (and_1_out, A, multiplexer_1_out);
  or or_1 (or_1_out, A, multiplexer_1_out);
  xor xor_1 (xor_1_out, A, multiplexer_1_out);
  one_bit_adder one_bit_adder_1 (.A(A), .B(multiplexer_1_out), .C_in(C_in), .S(one_bit_adder_1_s), .C_out(C_out));
  Multiplexer #(.enable("false"), .select(2)) multiplexer_2 (
    .in0(and_1_out), .in1(or_1_out), .in2(xor_1_out), .in3(one_bit_adder_1_s), .out(R), .sel(ALU_Ctrl[1:0]));
endmodule

module one_bit_adder (
  input  A,
  input  B,
  input  C_in,
  output S,
  output C_out
);

  wire and_1_out, and_2_out, xor_1_out;

  xor xor_1 (xor_1_out, A, B);
  and and_1 (and_1_out, xor_1_out, C_in);
  and and_2 (and_2_out, A, B);
  xor xor_2 (S, xor_1_out, C_in);
  or or_1 (C_out, and_1_out, and_2_out);
endmodule

module ALU_four (
  input  [3:0] ALU_Ctrl,
  input  [3:0] A,
  input  [3:0] B,
  input  C_in,
  output [3:0] R,
  output C_Out
);

  wire one_bit_alu_1_c_out, one_bit_alu_2_c_out, one_bit_alu_3_c_out;

  one_bit_ALU one_bit_alu_1 (
    .ALU_Ctrl(ALU_Ctrl), .A(A[0]), .B(B[0]), .C_in(C_in), .R(R[0]), .C_out(one_bit_alu_1_c_out));
  one_bit_ALU one_bit_alu_2 (
    .ALU_Ctrl(ALU_Ctrl), .A(A[1]), .B(B[1]), .C_in(one_bit_alu_1_c_out), .R(R[1]), .C_out(one_bit_alu_2_c_out));
  one_bit_ALU one_bit_alu_3 (
    .ALU_Ctrl(ALU_Ctrl), .A(A[2]), .B(B[2]), .C_in(one_bit_alu_2_c_out), .R(R[2]), .C_out(one_bit_alu_3_c_out));
  one_bit_ALU one_bit_alu_4 (
    .ALU_Ctrl(ALU_Ctrl), .A(A[3]), .B(B[3]), .C_in(one_bit_alu_3_c_out), .R(R[3]), .C_out(C_Out));
endmodule

module thirty_bit_ALU (
  input  [3:0] ALU_Ctrl,
  input  [31:0] A,
  input  [31:0] B,
  output [31:0] Result,
  output C_Out
);

  wire alu_four_1_c_out, alu_four_2_c_out, alu_four_3_c_out, alu_four_4_c_out, alu_four_5_c_out,
       alu_four_6_c_out, alu_four_7_c_out;

  ALU_four alu_four_1 (
    .ALU_Ctrl(ALU_Ctrl), .A(A[3:0]), .B(B[3:0]), .C_in(ALU_Ctrl[2]), .R(Result[3:0]), .C_Out(alu_four_1_c_out));
  ALU_four alu_four_2 (
    .ALU_Ctrl(ALU_Ctrl), .A(A[7:4]), .B(B[7:4]), .C_in(alu_four_1_c_out), .R(Result[7:4]),
    .C_Out(alu_four_2_c_out));
  ALU_four alu_four_3 (
    .ALU_Ctrl(ALU_Ctrl), .A(A[11:8]), .B(B[11:8]), .C_in(alu_four_2_c_out), .R(Result[11:8]),
    .C_Out(alu_four_3_c_out));
  ALU_four alu_four_4 (
    .ALU_Ctrl(ALU_Ctrl), .A(A[15:12]), .B(B[15:12]), .C_in(alu_four_3_c_out), .R(Result[15:12]),
    .C_Out(alu_four_4_c_out));
  ALU_four alu_four_5 (
    .ALU_Ctrl(ALU_Ctrl), .A(A[19:16]), .B(B[19:16]), .C_in(alu_four_4_c_out), .R(Result[19:16]),
    .C_Out(alu_four_5_c_out));
  ALU_four alu_four_6 (
    .ALU_Ctrl(ALU_Ctrl), .A(A[23:20]), .B(B[23:20]), .C_in(alu_four_5_c_out), .R(Result[23:20]),
    .C_Out(alu_four_6_c_out));
  ALU_four alu_four_7 (
    .ALU_Ctrl(ALU_Ctrl), .A(A[27:24]), .B(B[27:24]), .C_in(alu_four_6_c_out), .R(Result[27:24]),
    .C_Out(alu_four_7_c_out));
  ALU_four alu_four_8 (
    .ALU_Ctrl(ALU_Ctrl), .A(A[31:28]), .B(B[31:28]), .C_in(alu_four_7_c_out), .R(Result[31:28]), .C_Out(C_Out));
endmodule

module ALU_Control (
  input  i30,
  input  i14,
  input  i13,
  input  i12,
  input  i6,
  input  i5,
  input  i4,
  output aluCtrl3,
  output aluCtrl2,
  output aluCtrl1,
  output aluCtrl0,
  output aluSrc
);

  wire and_2_out, and_3_out, and_4_out, and_5_out, and_6_out, and_7_out, not_1_out, not_2_out, not_3_out,
       not_4_out, not_5_out, not_6_out, not_7_out;

  not not_1 (not_1_out, i30);
  not not_2 (not_2_out, i14);
  not not_3 (not_3_out, i13);
  not not_4 (not_4_out, i12);
  not not_5 (not_5_out, i6);
  not not_6 (not_6_out, i5);
  not not_7 (not_7_out, i4);
  and and_1 (aluCtrl2, i30, not_3_out, i5);
  or or_1 (aluCtrl1, not_3_out, not_7_out);
  and and_2 (and_2_out, i13, not_4_out, not_6_out);
  and and_3 (and_3_out, not_1_out, i13, not_4_out, not_5_out, i4);
  and and_4 (and_4_out, not_2_out, i13, not_4_out);
  and and_5 (and_5_out, i13, not_4_out, not_7_out);
  and and_6 (and_6_out, i13, not_4_out, i6);
  and and_7 (and_7_out, i30, i13, not_4_out);
  or or_2 (aluCtrl0, not_2_out, and_2_out, and_3_out);
  or or_3 (aluSrc, not_6_out, and_4_out, and_5_out, and_6_out, and_7_out);

  assign aluCtrl3 = 1'b0;
endmodule
